# Fritzing sketch functionGeneratorV2 (saved by Fritzing 0.9.3b)
circuit board: 1.7cm x 3.7cm
circuit board: 8cm x 12cm
breadboards: 1

parts:
  LCD1 = LCD screen
  Part1 = Arduino Nano (Rev3.0) (ICSP)
  RE1 = Rotary Encoder [package=THT]
  A = Screw terminal - 2 pins [package=THT]
  T = Screw terminal - 2 pins [package=THT]
  LED1 = LED - 3mm [color="Red (633nm)" package="3 mm [THT]"]
  R2 = Trimmer Potentiometer [maximum_resistance=50kΩ package=THT]
  B = Screw terminal - 2 pins [package=THT]
  R21 = Trimmer Potentiometer [maximum_resistance=20kΩ package=THT]
  R22 = Trimmer Potentiometer [maximum_resistance=2kΩ package=THT]
  R31 = Resistor [tolerance=±5% resistance=47k package="1206 [SMD]"]
  R18 = Resistor [tolerance=±1% resistance=15k package="0805 [SMD]"]
  R20 = Resistor [tolerance=±1% resistance=15k package="0805 [SMD]"]
  R16 = Resistor [tolerance=±1% resistance=15k package="0805 [SMD]"]
  R14 = Resistor [tolerance=±1% resistance=15k package="0805 [SMD]"]
  R12 = Resistor [tolerance=±1% resistance=15k package="0805 [SMD]"]
  R10 = Resistor [tolerance=±1% resistance=15k package="0805 [SMD]"]
  R8 = Resistor [tolerance=±1% resistance=15k package="0805 [SMD]"]
  R6 = Resistor [tolerance=±1% resistance=15k package="0805 [SMD]"]
  R5 = Resistor [tolerance=±1% resistance=7.5k package="1206 [SMD]"]
  R9 = Resistor [tolerance=±1% resistance=7.5k package="0603 [SMD]"]
  R11 = Resistor [tolerance=±1% resistance=7.5k package="0603 [SMD]"]
  R15 = Resistor [tolerance=±1% resistance=7.5k package="0603 [SMD]"]
  R17 = Resistor [tolerance=±1% resistance=7.5k package="0603 [SMD]"]
  R19 = Resistor [tolerance=±1% resistance=7.5k package="0603 [SMD]"]
  R7 = Resistor [tolerance=±1% resistance=7.5k package="1206 [SMD]"]
  U2 = LTC3105 [package=msop-12]
  S4 = SWITCH-MOMENTARY-2 [package=tactile-switch-1101ne]
  R1 = Resistor [tolerance=±1% resistance=15k package="0805 [SMD]"]
  R23 = Resistor [tolerance=±5% resistance=10k package="1206 [SMD]"]
  R = Screw terminal - 2 pins [package=THT]
  U4 = LM 358 Dual Op-Amp [package="DIP8 [THT]"]
  R32 = Resistor [tolerance=±5% resistance=1k package="0805 [SMD]"]
  C4 = Electrolytic Capacitor [capacitance=10µF voltage=50V package="100 mil [THT, electrolytic]"]
  J1 = female pin header, 4 pins [form="♀ (female)"]
  J2 = female pin header, 4 pins [form="♀ (female)"]

nets:
  GND: LCD1.VSS, LCD1.R/W, LCD1.LED-, Part1.GND, RE1.EncoderPinC, A.pin1, T.pin1, LED1.cathode, R2.leg1, B.pin1, R21.leg2, R12.Pin_1, U2.GND, S4.1, R23.Pin_1, R.pin1, U4.connector3, C4.-, J1.pin3, J1.pin4, J2.pin3, J2.pin4
  VDD: LCD1.VDD, Part1.5V, R21.leg1, R22.wiper, U2.VIN, J2.pin1
  N1: LCD1.V0, R21.wiper
  N2: LCD1.RS, Part1.A0
  N3: LCD1.E, Part1.A1
  N4: LCD1.DB4, Part1.A2
  N5: LCD1.DB5, Part1.A3
  N6: LCD1.DB6, Part1.A4
  N7: LCD1.DB7, Part1.A5
  N8: LCD1.LED+, R22.leg1
  N9: Part1.D1/TX, R6.Pin_1
  N10: Part1.D0/RX, R1.Pin_1
  N11: Part1.D2, R8.Pin_1
  N12: Part1.D3, R10.Pin_1
  N13: Part1.D4, R14.Pin_1
  N14: Part1.D5, R16.Pin_1
  N15: Part1.D6, R18.Pin_1
  N16: Part1.D7, R20.Pin_1
  N17: Part1.D9, T.pin2
  N18: Part1.D10, RE1.EncoderPinB
  N19: Part1.D11/MOSI, RE1.EncoderPinA
  N20: Part1.D12/MISO, S4.2
  N21: A.pin2, R31.Pin_0, U4.connector0
  N22: LED1.anode, R32.Pin_0
  N23: R2.wiper, U4.connector2, U4.connector4
  N24: R2.leg2, R20.Pin_0, R19.Pin_0, R.pin2
  N25: B.pin2, U4.connector5, U4.connector6, R32.Pin_1
  N26: R31.Pin_1, R23.Pin_0, U4.connector1
  N27: R18.Pin_0, R17.Pin_0, R19.Pin_1
  N28: R16.Pin_0, R15.Pin_0, R17.Pin_1
  N29: R14.Pin_0, R11.Pin_0, R15.Pin_1
  N30: R12.Pin_0, R5.Pin_1, R1.Pin_0
  N31: R10.Pin_0, R9.Pin_0, R11.Pin_1
  N32: R8.Pin_0, R9.Pin_1, R7.Pin_0
  N33: R6.Pin_0, R5.Pin_0, R7.Pin_1
  N34: U2.VOUT, U4.connector7, C4.+, J1.pin1

notes:
  7.5k in top row
  15k in bottom row
